// Logisim project Display de 7 segmentos.circ as structural Verilog
module Conversor_a (
  input  A,
  input  B,
  input  C,
  input  D,
  output a_2
);

  wire or_1_out, xnor_1_out;

  xnor xnor_1 (xnor_1_out, B, D);
  or or_1 (or_1_out, A, C);
  or or_2 (a_2, xnor_1_out, or_1_out);
endmodule

module Conversor_b (
  input  B,
  input  C,
  input  D,
  output out_4
);

  wire not_1_out, xnor_1_out;

  xnor xnor_1 (xnor_1_out, C, D);
  not not_1 (not_1_out, B);
  or or_1 (out_4, xnor_1_out, not_1_out);
endmodule

module Conversor_C (
  input  B,
  input  C,
  input  D,
  output c_2
);

  wire not_1_out;

  not not_1 (not_1_out, C);
  or or_1 (c_2, B, not_1_out, D);
endmodule

module Conversor_d (
  input  A,
  input  B,
  input  C,
  input  D,
  output d_2
);

  wire and_1_out, and_2_out, and_3_out, and_4_out, not_1_out, not_2_out, not_3_out, not_4_out, not_5_out;

  not not_1 (not_1_out, B);
  and and_1 (and_1_out, not_1_out, not_2_out);
  not not_2 (not_2_out, D);
  and and_2 (and_2_out, C, not_3_out);
  not not_3 (not_3_out, B);
  and and_3 (and_3_out, C, not_4_out);
  not not_4 (not_4_out, D);
  and and_4 (and_4_out, B, D, not_5_out);
  not not_5 (not_5_out, C);
  or or_1 (d_2, and_1_out, and_2_out, and_3_out, and_4_out, A);
endmodule

module Conversor_e (
  input  B,
  input  C,
  input  D,
  output e
);

  wire and_1_out, and_2_out, not_1_out, not_2_out, not_3_out;

  not not_1 (not_1_out, B);
  not not_2 (not_2_out, D);
  not not_3 (not_3_out, D);
  and and_1 (and_1_out, not_1_out, not_2_out);
  and and_2 (and_2_out, not_3_out, C);
  or or_1 (e, and_1_out, and_2_out);
endmodule

module Conversor_f (
  input  A,
  input  B,
  input  C,
  input  D,
  output f
);

  wire and_1_out, and_2_out, and_3_out, not_1_out, not_2_out, not_3_out, not_4_out;

  not not_1 (not_1_out, C);
  and and_1 (and_1_out, not_1_out, not_2_out);
  not not_2 (not_2_out, D);
  not not_3 (not_3_out, C);
  and and_2 (and_2_out, not_3_out, B);
  not not_4 (not_4_out, D);
  and and_3 (and_3_out, not_4_out, B);
  or or_1 (f, and_1_out, and_2_out, and_3_out, A);
endmodule

module Conversor_g (
  input  A,
  input  B,
  input  C,
  input  D,
  output g
);

  wire and_1_out, and_2_out, and_3_out, not_1_out, not_2_out, not_3_out;

  and and_1 (and_1_out, C, not_1_out);
  not not_1 (not_1_out, D);
  not not_2 (not_2_out, C);
  and and_2 (and_2_out, not_2_out, B);
  not not_3 (not_3_out, B);
  and and_3 (and_3_out, not_3_out, C);
  or or_1 (g, and_1_out, and_2_out, and_3_out, A);
endmodule

module MACRO (
  input  [3:0] in_1,
  output g,
  output f,
  output a,
  output b,
  output c,
  output d,
  output e
);

  Conversor_a conversor_a_1 (.A(in_1[3]), .B(in_1[2]), .C(in_1[1]), .D(in_1[0]), .a_2(a));
  Conversor_b conversor_b_1 (.B(in_1[2]), .C(in_1[1]), .D(in_1[0]), .out_4(b));
  Conversor_d conversor_d_1 (.A(in_1[3]), .B(in_1[2]), .C(in_1[1]), .D(in_1[0]), .d_2(d));
  Conversor_C conversor_c_1 (.B(in_1[2]), .C(in_1[1]), .D(in_1[0]), .c_2(c));
  Conversor_e conversor_e_1 (.B(in_1[2]), .C(in_1[1]), .D(in_1[0]), .e(e));
  Conversor_f conversor_f_1 (.A(in_1[3]), .B(in_1[2]), .C(in_1[1]), .D(in_1[0]), .f(f));
  Conversor_g conversor_g_1 (.A(in_1[3]), .B(in_1[2]), .C(in_1[1]), .D(in_1[0]), .g(g));

  // Notes on the sheet:
  //   a
  //   b
  //   c
  //   d
  //   e
  //   f
  //   g
endmodule

module Display_de_7_Segmentos (
);

  wire clock_1_out, macro_1_a, macro_1_b, macro_1_c, macro_1_d, macro_1_e, macro_1_f, macro_1_g;
  wire [3:0] counter_1_q;

  Clock clock_1 (.out(clock_1_out));
  Counter #(.width(4), .max('h9)) counter_1 (.Q(counter_1_q), .clk(clock_1_out));  // open: load, D, count, carry, clr
  MACRO macro_1 (
    .in_1(counter_1_q), .g(macro_1_g), .f(macro_1_f), .a(macro_1_a), .b(macro_1_b), .c(macro_1_c),
    .d(macro_1_d), .e(macro_1_e));
  _7_Segment_Display u_7_segment_display_1 (
    .g(macro_1_g), .f(macro_1_f), .a(macro_1_a), .b(macro_1_b), .e(macro_1_e), .d(macro_1_d), .c(macro_1_c));  // open: dp
endmodule
