// Logisim project Projeto Subtração.circ as structural Verilog: 5 circuits, main circuit main
module main (
  input  [3:0] in_1,
  input  [3:0] in_2,
  output [3:0] out_3
);

  Sub sub_1 (.out_3(out_3), .in_1(in_1), .in_2(in_2));
endmodule

module ADD_1 (
  input  A,
  input  B,
  input  Vem_1,
  output S,
  output Vai_1
);

  wire and_1_out, and_2_out, or_1_out, xor_1_out;

  xor xor_1 (xor_1_out, B, A);
  or or_1 (or_1_out, Vem_1, B);
  and and_1 (and_1_out, B, Vem_1);
  and and_2 (and_2_out, or_1_out, A);
  xor xor_2 (S, Vem_1, xor_1_out);
  or or_2 (Vai_1, and_2_out, and_1_out);
endmodule

module ADD_4 (
  input  [3:0] in_1,
  input  [3:0] in_2,
  output out_3,
  output [3:0] out_4
);

  wire add_1_2_vai_1, add_1_3_vai_1, add_1_4_vai_1;

  ADD_1 add_1_1 (.S(out_4[3]), .Vai_1(out_3), .A(in_2[3]), .B(in_1[3]), .Vem_1(add_1_3_vai_1));
  ADD_1 add_1_2 (.S(out_4[1]), .Vai_1(add_1_2_vai_1), .A(in_2[1]), .B(in_1[1]), .Vem_1(add_1_4_vai_1));
  ADD_1 add_1_3 (.S(out_4[2]), .Vai_1(add_1_3_vai_1), .A(in_2[2]), .B(in_1[2]), .Vem_1(add_1_2_vai_1));
  ADD_1 add_1_4 (.S(out_4[0]), .Vai_1(add_1_4_vai_1), .A(in_2[0]), .B(in_1[0]), .Vem_1(1'b0));
endmodule

module COMP_2 (
  input  [3:0] in_1,
  output [3:0] out_2
);

  wire [3:0] not_4_out;

  not not_1 (not_4_out[3], in_1[3]);
  not not_2 (not_4_out[1], in_1[1]);
  not not_3 (not_4_out[2], in_1[2]);
  not not_4 (not_4_out[0], in_1[0]);
  ADD_4 add_4_1 (.in_2(not_4_out), .in_1(4'b0001), .out_4(out_2));  // open: out_3
endmodule

module Sub (
  input  [3:0] in_1,
  input  [3:0] in_2,
  output [3:0] out_3
);

  wire [3:0] comp_2_1_out_2;

  COMP_2 comp_2_1 (.in_1(in_2), .out_2(comp_2_1_out_2));
  ADD_4 add_4_1 (.in_2(in_1), .in_1(comp_2_1_out_2), .out_4(out_3));  // open: out_3
endmodule
